# Fritzing sketch krypton_circuit (saved by Fritzing 1.0.6)

parts:
  A1 = ESP32-S3 devkit 1
  433T30D1 = 433T30D

nets:
  N1: A1.Pin_1, 433T30D1.M0, 433T30D1.M1, 433T30D1.GND
  N2: A1.Pin_2, 433T30D1.VCC
  N3: A1.Pin_9, 433T30D1.AUX
  N4: A1.Pin_10, 433T30D1.TXD
  N5: A1.Pin_11, 433T30D1.RXD

custom parts:
  ESP32-S3 devkit 1: ESP32-S3-DevKitC-1 Development Board BT 2.4G Wifi Module for Arduino 8MB PSRAM 16MB FLASH N16R8 42Pin CH340C Type-C ESP32 S3.
  433T30D: Long Distance Wireless Transceiver UART LoRa Module
